// Digital circuit CPU.dig as structural Verilog
module CPU (
  input  [16:0] PRGMR_A,
  input  PRMGR_ACT,
  input  [7:0] PRMR_DATA,
  input  PRMR_WE,
  input  clk,
  input  [15:0] TEST_DATA,
  input  TEST_SEND
);

  wire and_1_out, and_2_out, and_3_out, bus_debugger_1_fb, CONT, decoder_1_out_0, decoder_1_out_2,
       decoder_1_out_3, decoder_1_out_4, IF_EN, instruction_decoder_1_p4, instruction_decoder_1_p10,
       or_1_out, or_2_out, or_3_out, or_4_out, RST;
  wire [0:0] decoder_1_out_1;
  wire [2:0] bus_debugger_1_last_addr_out, counter_1_out;
  wire [3:0] driver_1_out, instruction_decoder_1_p7, instruction_decoder_1_p8, instruction_decoder_1_p9;
  wire [7:0] GLS29EE010_70_4C_PHE__EEPROM_d, LOW_INS_q;
  wire [15:0] bus_debugger_1_last_data_out, DATA_READ, DATA_READ_IF, DATA_WRITE, driver_2_out,
       registers_1_data_read, registers_1_pc_out, undriven;
  wire [15:8] HIGH_INS_q;
  wire [16:0] driverinvsel_3_out;

  assign driver_1_out = IF_EN ? instruction_decoder_1_p9 : 4'bz;  // Driver driver_1
  assign driver_1_out = ~IF_EN ? instruction_decoder_1_p7 : 4'bz;  // DriverInvSel driverinvsel_1
  assign driver_2_out = bus_debugger_1_fb ? undriven : 16'bz;  // Driver driver_2
  PullDown #(.Bits(4)) pulldown_1 (.out(driver_1_out));
  Registers registers_1 (
    .ADDR_READ(driver_1_out), .ADDR_WRITE(instruction_decoder_1_p8), .DATA_WRITE(DATA_WRITE), .CLK(clk),
    .WRITE_ENABLE(instruction_decoder_1_p10), .BUS_DATA_IN(driver_2_out), .FROM_BUS_IN(bus_debugger_1_fb),
    .PC_INC(decoder_1_out_4), .RESET(RST), .DATA_READ(registers_1_data_read), .PC_OUT(registers_1_pc_out));
  assign DATA_READ_IF = IF_EN ? registers_1_data_read : 16'bz;  // Driver driver_3
  assign DATA_READ = ~IF_EN ? registers_1_data_read : 16'bz;  // DriverInvSel driverinvsel_2
  Bus_Debugger bus_debugger_1 (
    .DATA(undriven), .ADDR(3'b000), .TB(1'b0), .TEST_DATA(TEST_DATA), .TEST_SEND(TEST_SEND), .CLK(clk),
    .FB(bus_debugger_1_fb), .LAST_DATA_OUT(bus_debugger_1_last_data_out),
    .LAST_ADDR_OUT(bus_debugger_1_last_addr_out));
  // Probe CLK on clk
  Reset_On_First_Clock reset_on_first_clock_1 (.CLK(clk), .RST(RST));
  assign driverinvsel_3_out = ~PRMGR_ACT ? {registers_1_pc_out, decoder_1_out_1[0]} : 17'bz;  // DriverInvSel driverinvsel_3
  PullDown pulldown_2 (.out(PRMGR_ACT));
  or or_1 (or_1_out, RST, decoder_1_out_4);
  LED led_1 (.in(bus_debugger_1_last_data_out[1]));
  LED led_2 (.in(bus_debugger_1_last_data_out[0]));
  LED led_3 (.in(bus_debugger_1_last_data_out[2]));
  or or_2 (or_2_out, decoder_1_out_0, decoder_1_out_1[0], CONT, decoder_1_out_3);
  Counter #(.Bits(3)) counter_1 (.en(or_2_out), .C(clk), .clr(or_1_out), .out(counter_1_out));  // open: ovf
  assign driverinvsel_3_out = PRMGR_ACT ? PRGMR_A : 17'bz;  // Driver driver_4
  LED led_4 (.in(bus_debugger_1_last_data_out[3]));
  LED led_5 (.in(bus_debugger_1_last_data_out[5]));
  LED led_6 (.in(bus_debugger_1_last_data_out[4]));
  LED led_7 (.in(bus_debugger_1_last_data_out[6]));
  PullDown pulldown_3 (.out(PRMR_WE));
  LED led_8 (.in(bus_debugger_1_last_data_out[7]));
  LED led_9 (.in(bus_debugger_1_last_data_out[9]));
  LED led_10 (.in(bus_debugger_1_last_data_out[8]));
  LED led_11 (.in(bus_debugger_1_last_data_out[10]));
  Decoder #(.Selector_Bits(3)) decoder_1 (
    .sel(counter_1_out), .out_0(decoder_1_out_0), .out_1(decoder_1_out_1[0]), .out_2(decoder_1_out_2),
    .out_3(decoder_1_out_3), .out_4(decoder_1_out_4));  // open: out_5, out_6, out_7
  LED led_12 (.in(bus_debugger_1_last_data_out[11]));
  LED led_13 (.in(bus_debugger_1_last_data_out[13]));
  LED led_14 (.in(bus_debugger_1_last_data_out[12]));
  LED led_15 (.in(bus_debugger_1_last_data_out[14]));
  EEPROM #(.AddrBits(17), .Bits(8)) GLS29EE010_70_4C_PHE__EEPROM (
    .A(driverinvsel_3_out), .CS(1'b1), .WE(PRMR_WE), .OE(~PRMGR_ACT), .D(GLS29EE010_70_4C_PHE__EEPROM_d));
  LED led_16 (.in(bus_debugger_1_last_data_out[15]));
  LED led_17 (.in(bus_debugger_1_last_addr_out[0]));
  or or_3 (or_3_out, decoder_1_out_3, RST, decoder_1_out_2);
  LED led_18 (.in(bus_debugger_1_last_addr_out[1]));
  LED led_19 (.in(bus_debugger_1_last_addr_out[2]));
  assign GLS29EE010_70_4C_PHE__EEPROM_d = PRMGR_ACT ? PRMR_DATA : 8'bz;  // Driver driver_5
  D_FF #(.Bits(8)) HIGH_INS (.D(GLS29EE010_70_4C_PHE__EEPROM_d), .C(and_1_out), .Q(HIGH_INS_q));  // open: nQ
  and and_1 (and_1_out, clk, decoder_1_out_0);
  and and_2 (and_2_out, or_3_out, clk);
  D_FF #(.Bits(8)) LOW_INS (.D(GLS29EE010_70_4C_PHE__EEPROM_d), .C(and_3_out), .Q(LOW_INS_q));  // open: nQ
  and and_3 (and_3_out, ~clk, decoder_1_out_1[0]);  // And
  or or_4 (or_4_out, CONT, decoder_1_out_3, RST);
  // Instruction_Decoder instruction_decoder_1: pin names not known; wires that end beside it: {HIGH_INS_q, LOW_INS_q}, and_2_out, or_4_out, instruction_decoder_1_p4, CONT, IF_EN, instruction_decoder_1_p7, instruction_decoder_1_p8, instruction_decoder_1_p9, instruction_decoder_1_p10
  LED led_20 (.in(instruction_decoder_1_p4));
  assign DATA_WRITE = CONT ? DATA_READ : 16'bz;  // Driver driver_6

  // Notes on the sheet:
  //   clk: Hz: 50
  //   0: INS_LOAD_LOW
  //   1: INS_LOAD_HIGH
  //   2: WAITING_FOR_INS_EXEC
  //   3: CLEANUP
  //   4: PC_INCREMENT
  //   contents of GLS29EE010_70_4C_PHE__EEPROM (hex, n*v repeats v):
  //   b,e1
  //   HALTED
endmodule
